# Fritzing sketch fritzing (saved by Fritzing 0.9.3b)

parts:
  LCD1602_I2C = LCD1602-I2C
  PMS5003_Sensor1 = Plantower PMS5003
  Part3 = Seeeduino V3.0

nets:
  GND: LCD1602_I2C.GND, PMS5003_Sensor1.GND, Part3.GND
  VCC: LCD1602_I2C.VCC, PMS5003_Sensor1.VCC, Part3.5V
  N1: LCD1602_I2C.SDA, Part3.A4
  N2: LCD1602_I2C.SCL, Part3.A5, Part3.SCL
  N3: PMS5003_Sensor1.RXD, Part3.D1/TX
  N4: PMS5003_Sensor1.TXD, Part3.D0/RX, Part3.RX

custom parts:
  LCD1602-I2C: A standard character display, usually with 2x16 characters. Comes in many colors with LCM1602 IIC attached.
  Plantower PMS5003: Particulate Matter Sensor
